# Fritzing sketch MultiSensor (saved by Fritzing 0.7.10b)
breadboards: 1

parts:
  Arduino1 = Arduino
  T1 = LM35 Temperature Sensor [package="TO92 [THT]"]
  S1 = Pushbutton [package="[THT]"]
  R1 = Resistor [tolerance=±5% resistance=10k package=THT]
  LCD1 = LCD screen
  SENSOR1 = MPL115A2 Barometer Breakout Board
  Part1 = Tri-Axis Gyro Breakout - L3G4200D
  HMC5883L = Triple Axis Magnetometer - HMC5883 Breakout

nets:
  N1: Arduino1.D8, S1.Pin_3, S1.Pin_4, R1.Pin_0
  N2: Arduino1.D7, LCD1.VSS
  VDD: Arduino1.+5V, T1.+Vs, S1.Pin_1, S1.Pin_2, LCD1.VDD, SENSOR1.VDD, Part1.VCC, HMC5883L.SDA
  GND: Arduino1.GND, T1.GND, R1.Pin_1, LCD1.V0, SENSOR1.GND, Part1.GND, Part1.SDO, HMC5883L.SCL
  N3: Arduino1.A0, T1.Vout
  N4: Arduino1.A4, SENSOR1.SDA, Part1.SDA, HMC5883L.GND
  N5: Arduino1.A5, SENSOR1.SCL, Part1.SCL, HMC5883L.VCC

notes:
  MultiSensor
  SCL - Brown wire
  SDA - Purple wire
  Use serial LCD
  RX - Gray wire
  Parallax breakout is 5 pins. Middle pin unused.

custom parts:
  MPL115A2 Barometer Breakout Board: MPL115A2 I2C Barometric Sensor
