# Fritzing sketch schematic (saved by Fritzing 0.7.10b)
breadboards: 1

parts:
  Arduino1 = Arduino
  LED1 = RGB LED (com. anode, rbg) [package="5 mm [THT]"]
  R1 = Resistor [tolerance=±5% resistance=220 package=THT]
  R2 = Resistor [tolerance=±5% resistance=220 package=THT]
  part = Resistor [tolerance=±5% resistance=220 package=THT]
  560Ω_(3) = Resistor [tolerance=±5% resistance=220 package=THT]  # not connected
  RGB_LED_(red_anode_blue_green) = RGB LED (com. anode, rbg) [package="5 mm [THT]"]  # not connected

nets:
  N1: Arduino1.D11, R1.Pin_1
  N2: Arduino1.D10, part.Pin_1
  N3: Arduino1.D9, R2.Pin_1
  N4: LED1.red_cathode, R1.Pin_0
  N5: LED1.blue_cathode, R2.Pin_0
  N6: LED1.green_cathode, part.Pin_0
